// Logisim project CPU.circ as structural Verilog
module ALU (
  input  [31:0] RS,
  input  [31:0] RT,
  input  [3:0] ALUop,
  output [31:0] Rezultat,
  output Zero
);

  wire comparator_1_lt;
  wire [31:0] adder_1_out, and_1_out, bit_extender_1_out, or_1_out, subtractor_1_out;

  assign and_1_out = RS & RT;  // AND_Gate and_1, 32 bits wide
  assign or_1_out = RS | RT;  // OR_Gate or_1, 32 bits wide
  Adder #(.width(32)) adder_1 (.a(RS), .b(RT), .out(adder_1_out));  // open: cin, cout
  Subtractor #(.width(32)) subtractor_1 (.a(RS), .b(RT), .out(subtractor_1_out));  // open: bin, bout
  Comparator #(.width(32)) comparator_1 (.a(RS), .b(RT), .lt(comparator_1_lt));  // open: gt, eq
  assign bit_extender_1_out = {{31{1'b0}}, comparator_1_lt};  // Bit_Extender bit_extender_1
  Multiplexer #(.select(4), .width(32), .enable("false")) multiplexer_1 (
    .in0(and_1_out), .in1(or_1_out), .in2(adder_1_out), .in6(subtractor_1_out), .in7(bit_extender_1_out),
    .out(Rezultat), .sel(ALUop));  // open: in3, in4, in5, in8, in9, in10, in11, in12, in13, in14, in15
  Comparator #(.width(32)) comparator_2 (.a(Rezultat), .b({32{1'b0}}), .eq(Zero));  // open: gt, lt
endmodule

module ALU_Control (
  input  [1:0] ALUOP,
  input  [5:0] FUNCTION,
  output [3:0] Rezultat
);

  wire and_1_out, and_2_out, and_3_out, and_4_out, and_5_out, and_6_out, and_7_out, and_8_out, and_9_out,
       and_10_out, and_11_out, and_12_out, and_13_out, and_14_out, not_1_out, not_2_out, not_3_out,
       not_4_out, not_5_out, not_6_out, not_7_out, not_8_out, not_9_out, not_10_out, not_11_out, not_12_out,
       not_13_out, not_14_out, not_15_out, not_16_out, not_17_out, not_18_out, not_19_out, or_2_out;

  not not_1 (not_1_out, ALUOP[1]);
  not not_2 (not_2_out, ALUOP[0]);
  not not_3 (not_3_out, FUNCTION[1]);
  not not_4 (not_4_out, FUNCTION[3]);
  not not_5 (not_5_out, FUNCTION[4]);
  not not_6 (not_6_out, FUNCTION[0]);
  not not_7 (not_7_out, FUNCTION[2]);
  not not_8 (not_8_out, FUNCTION[4]);
  not not_9 (not_9_out, FUNCTION[0]);
  not not_10 (not_10_out, FUNCTION[2]);
  not not_11 (not_11_out, FUNCTION[3]);
  not not_12 (not_12_out, FUNCTION[4]);
  not not_13 (not_13_out, FUNCTION[1]);
  not not_14 (not_14_out, FUNCTION[0]);
  not not_15 (not_15_out, FUNCTION[3]);
  not not_16 (not_16_out, FUNCTION[4]);
  not not_17 (not_17_out, FUNCTION[1]);
  not not_18 (not_18_out, FUNCTION[4]);
  not not_19 (not_19_out, FUNCTION[4]);
  and and_1 (and_1_out, ALUOP[0], not_1_out);
  and and_2 (and_2_out, not_2_out, ALUOP[1]);
  and and_3 (and_3_out, FUNCTION[0], not_3_out, FUNCTION[2], not_4_out, not_5_out, FUNCTION[5]);
  and and_4 (and_4_out, FUNCTION[1], FUNCTION[3], FUNCTION[5], not_6_out, not_7_out, not_8_out);
  and and_5 (and_5_out, FUNCTION[1], FUNCTION[5], not_9_out, not_10_out, not_11_out, not_12_out);
  and and_6 (and_6_out, not_13_out, FUNCTION[5], not_14_out, FUNCTION[2], not_15_out, not_16_out);
  and and_7 (and_7_out, FUNCTION[5], FUNCTION[0], FUNCTION[2], not_17_out, not_18_out, not_19_out);
  and and_8 (and_8_out, and_2_out, and_3_out);
  and and_9 (and_9_out, and_2_out, and_4_out);
  buf and_10 (and_10_out, and_1_out);  // AND_Gate
  and and_11 (and_11_out, and_2_out, and_5_out);
  and and_12 (and_12_out, and_2_out, and_4_out);
  and and_13 (and_13_out, and_2_out, and_6_out);
  and and_14 (and_14_out, and_2_out, and_7_out);
  or or_1 (Rezultat[0], and_8_out, and_9_out);
  or or_2 (or_2_out, and_13_out, and_14_out);
  or or_3 (Rezultat[2], and_10_out, and_12_out, and_11_out);
  not not_20 (Rezultat[1], or_2_out);

  assign Rezultat[3] = 1'b0;
endmodule

module Bus (
  input  [31:0] in_1,
  output [5:0] Function,
  output [4:0] Write_reg,
  output [4:0] Reg2,
  output [4:0] Reg1,
  output [5:0] OP,
  output [31:0] Lower_16_SE
);

  assign Lower_16_SE = {{16{in_1[15]}}, in_1[15:0]};  // Bit_Extender bit_extender_1

  assign Function = in_1[5:0];
  assign OP = in_1[31:26];
  assign Reg1 = in_1[25:21];
  assign Reg2 = in_1[20:16];
  assign Write_reg = in_1[15:11];
endmodule

module \Upravljački_sklop  (
  input  [5:0] in_1,
  output RegDst,
  output jmp,
  output Branch,
  output RegWrite,
  output ALUsrc,
  output MemRead,
  output MemWrite,
  output MemtoReg,
  output [1:0] OP
);

  wire and_6_out, not_1_out, not_2_out, not_3_out, not_4_out, not_5_out, not_6_out, not_7_out, not_8_out,
       not_9_out, not_10_out, not_11_out, not_12_out, not_13_out, not_14_out, not_15_out, not_16_out,
       not_17_out, not_18_out, not_19_out, not_20_out, not_21_out, not_22_out, not_23_out, not_24_out,
       not_25_out;

  not not_1 (not_1_out, in_1[0]);
  not not_2 (not_2_out, in_1[1]);
  not not_3 (not_3_out, in_1[2]);
  not not_4 (not_4_out, in_1[3]);
  not not_5 (not_5_out, in_1[4]);
  not not_6 (not_6_out, in_1[5]);
  not not_7 (not_7_out, in_1[2]);
  and and_1 (MemRead, in_1[0], in_1[1], not_7_out, not_8_out, not_9_out, in_1[5]);
  not not_8 (not_8_out, in_1[3]);
  not not_9 (not_9_out, in_1[4]);
  not not_10 (not_10_out, in_1[2]);
  and and_2 (MemWrite, in_1[0], in_1[1], not_10_out, in_1[3], not_11_out, in_1[5]);
  not not_11 (not_11_out, in_1[4]);
  not not_12 (not_12_out, in_1[0]);
  not not_13 (not_13_out, in_1[1]);
  and and_3 (Branch, not_12_out, not_13_out, in_1[2], not_14_out, not_15_out, not_16_out);
  not not_14 (not_14_out, in_1[3]);
  not not_15 (not_15_out, in_1[4]);
  not not_16 (not_16_out, in_1[5]);
  not not_17 (not_17_out, in_1[0]);
  not not_18 (not_18_out, in_1[2]);
  not not_19 (not_19_out, in_1[3]);
  and and_4 (jmp, not_17_out, in_1[1], not_18_out, not_19_out, not_20_out, not_21_out);
  not not_20 (not_20_out, in_1[4]);
  not not_21 (not_21_out, in_1[5]);
  not not_22 (not_22_out, in_1[1]);
  not not_23 (not_23_out, in_1[2]);
  not not_24 (not_24_out, in_1[4]);
  not not_25 (not_25_out, in_1[5]);
  and and_5 (OP[1], not_1_out, not_2_out, not_3_out, not_4_out, not_5_out, not_6_out);
  and and_6 (and_6_out, in_1[0], not_22_out, not_23_out, in_1[3], not_24_out, not_25_out);
  or or_1 (ALUsrc, MemWrite, and_6_out, MemRead);
  or or_2 (RegWrite, OP[1], and_6_out, MemRead);

  assign MemtoReg = MemRead;
  assign OP[0] = Branch;
  assign RegDst = OP[1];
endmodule

module Register_file (
  input  [4:0] RR1,
  input  [4:0] RR2,
  input  [4:0] WR,
  input  [31:0] W_DATA,
  input  in_5,
  output [31:0] RR1_2,
  output [31:0] RR2_2
);

  wire decoder_1_out0, decoder_1_out1, decoder_1_out2, decoder_1_out3, decoder_1_out4, decoder_1_out5,
       decoder_1_out6, decoder_1_out7;
  wire [31:0] register_1_q, register_2_q, register_3_q, register_4_q, register_5_q, register_6_q,
       register_7_q, register_8_q;

  Decoder #(.select(3)) decoder_1 (
    .out0(decoder_1_out0), .out1(decoder_1_out1), .out2(decoder_1_out2), .out3(decoder_1_out3),
    .out4(decoder_1_out4), .out5(decoder_1_out5), .out6(decoder_1_out6), .out7(decoder_1_out7), .sel(WR[2:0]));  // open: en
  Register #(.width(32), .trigger("falling")) register_1 (
    .D(W_DATA), .en(decoder_1_out0), .Q(register_1_q), .clk(in_5));  // open: clr
  Register #(.width(32), .trigger("falling")) register_2 (
    .D(W_DATA), .en(decoder_1_out1), .Q(register_2_q), .clk(in_5));  // open: clr
  Register #(.width(32), .trigger("falling")) register_3 (
    .D(W_DATA), .en(decoder_1_out2), .Q(register_3_q), .clk(in_5));  // open: clr
  Register #(.width(32), .trigger("falling")) register_4 (
    .D(W_DATA), .en(decoder_1_out3), .Q(register_4_q), .clk(in_5));  // open: clr
  Register #(.width(32), .trigger("falling")) register_5 (
    .D(W_DATA), .en(decoder_1_out4), .Q(register_5_q), .clk(in_5));  // open: clr
  Register #(.width(32), .trigger("falling")) register_6 (
    .D(W_DATA), .en(decoder_1_out5), .Q(register_6_q), .clk(in_5));  // open: clr
  Register #(.width(32), .trigger("falling")) register_7 (
    .D(W_DATA), .en(decoder_1_out6), .Q(register_7_q), .clk(in_5));  // open: clr
  Register #(.width(32), .trigger("falling")) register_8 (
    .D(W_DATA), .en(decoder_1_out7), .Q(register_8_q), .clk(in_5));  // open: clr
  Multiplexer #(.select(3), .width(32)) multiplexer_1 (
    .in0(register_1_q), .in1(register_2_q), .in2(register_3_q), .in3(register_4_q), .in4(register_5_q),
    .in5(register_6_q), .in6(register_7_q), .in7(register_8_q), .out(RR1_2), .sel(RR1[2:0]), .en(1'b1));
  Multiplexer #(.select(3), .width(32)) multiplexer_2 (
    .in0(register_1_q), .in1(register_2_q), .in2(register_3_q), .in3(register_4_q), .in4(register_5_q),
    .in5(register_6_q), .in6(register_7_q), .in7(register_8_q), .out(RR2_2), .sel(RR2[2:0]), .en(1'b1));
endmodule

module \Sklop_za_izračun_adrese  (
  input  [31:0] _16SE,
  input  [2:0] PC_1,
  input  B,
  input  Z,
  input  J,
  output [2:0] Izlaz_iz_PCC
);

  wire and_1_out;
  wire [2:0] adder_1_out, multiplexer_1_out;

  Adder #(.width(3)) adder_1 (.a(_16SE[2:0]), .b(PC_1), .out(adder_1_out));  // open: cin, cout
  and and_1 (and_1_out, B, Z);
  Multiplexer #(.width(3), .enable("false")) multiplexer_1 (
    .in0(PC_1), .in1(adder_1_out), .out(multiplexer_1_out), .sel(and_1_out));
  Multiplexer #(.width(3), .enable("false")) multiplexer_2 (
    .in0(multiplexer_1_out), .in1(_16SE[2:0]), .out(Izlaz_iz_PCC), .sel(J));
endmodule

module Procesor (
);

  wire ALU_zero, and_1_out, and_2_out, clock_1_out, Main_control_alusrc, Main_control_branch,
       Main_control_jmp, Main_control_memtoreg, Main_control_memwrite, Main_control_regdst,
       Main_control_regwrite;
  wire [1:0] Main_control_op;
  wire [2:0] adder_1_out, \Izračun_adrese_izlaz_iz_pcc , PC_q;
  wire [3:0] Alu_control_rezultat;
  wire [4:0] Bus_reg1, Bus_reg2, Bus_write_reg, multiplexer_1_out;
  wire [5:0] Bus_function, Bus_op;
  wire [31:0] ALU_rezultat, Bus_lower_16_se, multiplexer_2_out, multiplexer_3_out, ram_1_data, ram_2_data,
       Register_file_rr1_2, Register_file_rr2_2;

  Clock clock_1 (.out(clock_1_out));
  Register #(.width(3), .trigger("falling")) PC (
    .D(\Izračun_adrese_izlaz_iz_pcc ), .Q(PC_q), .clk(clock_1_out));  // open: en, clr
  Adder #(.width(3)) adder_1 (.a(PC_q), .b(3'b001), .out(adder_1_out));  // open: cin, cout
  RAM #(.addrWidth(3), .dataWidth(32)) ram_1 (.addr(PC_q), .data(ram_1_data));  // open: sel, clk, ld, clr
  Bus Bus (
    .in_1(ram_1_data), .Function(Bus_function), .Write_reg(Bus_write_reg), .Reg2(Bus_reg2), .Reg1(Bus_reg1),
    .OP(Bus_op), .Lower_16_SE(Bus_lower_16_se));
  \Upravljački_sklop  Main_control (
    .in_1(Bus_op), .RegDst(Main_control_regdst), .jmp(Main_control_jmp), .Branch(Main_control_branch),
    .RegWrite(Main_control_regwrite), .ALUsrc(Main_control_alusrc), .MemWrite(Main_control_memwrite),
    .MemtoReg(Main_control_memtoreg), .OP(Main_control_op));  // open: MemRead
  Register_file Register_file (
    .RR1(Bus_reg1), .RR2(Bus_reg2), .WR(multiplexer_1_out), .W_DATA(multiplexer_3_out), .in_5(and_1_out),
    .RR1_2(Register_file_rr1_2), .RR2_2(Register_file_rr2_2));
  Multiplexer #(.width(5), .enable("false")) multiplexer_1 (
    .in0(Bus_reg2), .in1(Bus_write_reg), .out(multiplexer_1_out), .sel(Main_control_regdst));
  and and_1 (and_1_out, clock_1_out, Main_control_regwrite);
  ALU_Control Alu_control (.ALUOP(Main_control_op), .FUNCTION(Bus_function), .Rezultat(Alu_control_rezultat));
  Multiplexer #(.width(32)) multiplexer_2 (
    .in0(Register_file_rr2_2), .in1(Bus_lower_16_se), .out(multiplexer_2_out), .sel(Main_control_alusrc));  // open: en
  \Sklop_za_izračun_adrese  \Izračun_adrese  (
    ._16SE(Bus_lower_16_se), .PC_1(adder_1_out), .B(Main_control_branch), .Z(ALU_zero), .J(Main_control_jmp),
    .Izlaz_iz_PCC(\Izračun_adrese_izlaz_iz_pcc ));
  ALU ALU (
    .RS(Register_file_rr1_2), .RT(multiplexer_2_out), .ALUop(Alu_control_rezultat), .Rezultat(ALU_rezultat),
    .Zero(ALU_zero));
  and and_2 (and_2_out, Main_control_memwrite, clock_1_out);
  RAM #(.dataWidth(32), .bus("separate")) ram_2 (
    .addr(ALU_rezultat[7:0]), .din(Register_file_rr2_2), .data(ram_2_data), .clk(and_2_out));  // open: str, sel, ld, clr
  Multiplexer #(.width(32)) multiplexer_3 (
    .in0(ALU_rezultat), .in1(ram_2_data), .out(multiplexer_3_out), .sel(Main_control_memtoreg));  // open: en

  // Notes on the sheet:
  //   Instruction memory
  //   RAM
endmodule

module Instrukcijska_memorija (
);

  wire clock_1_out;
  wire [2:0] adder_1_out, register_1_q;
  wire [31:0] ram_1_data;

  Clock clock_1 (.out(clock_1_out));
  Adder #(.width(3)) adder_1 (.a(register_1_q), .b(3'b001), .out(adder_1_out));  // open: cin, cout
  Register #(.width(3)) register_1 (.D(adder_1_out), .Q(register_1_q), .clk(clock_1_out));  // open: en, clr
  RAM #(.addrWidth(3), .dataWidth(32)) ram_1 (.addr(register_1_q), .data(ram_1_data));  // open: sel, clk, ld, clr
endmodule
